# Fritzing sketch v2_attiny_RGB_3V (saved by Fritzing 0.9.10b)
circuit board: 6.1cm x 3.2cm
breadboards: 1

parts:
  R1 = Resistor [tolerance=±5% power=0.25 resistance=100 mn=100Ω package=THT]
  R2 = Resistor [tolerance=±5% power=0.25 resistance=100 mn=100Ω package=THT]
  R3 = Resistor [tolerance=±5% power=0.25 resistance=100 mn=100Ω package=THT]
  LED1 = RGB LED (com. anode, rbg) [mn="rgb led " mpn="cmn anode" package="5 mm [THT]"]
  U1 = ATTINY45 [mn=ATtiny85 package=dip]
  R4 = Rotary Potentiometer (Small) [maximum_resistance=100kΩ knob_status=50% power=0.5W mn="JIJ BENT M" package=THT]
  J1 = Screw terminal - 2 pins [mn="-   +" mpn=3V package=THT]
  S2 = SWITCH-MOMENTARY-2 [mn="RGB BOARD" mpn=artechlab package=tactile-pth]

nets:
  N1: R1.Pin_0, LED1.green_cathode
  N2: R1.Pin_1, U1.PB4(ADC2)
  N3: R2.Pin_0, LED1.blue_cathode
  N4: R2.Pin_1, U1.PB1(MISO)
  N5: R3.Pin_0, LED1.red_cathode
  N6: R3.Pin_1, U1.PB0(MOSI)
  N7: LED1.common_anode, U1.VCC, R4.leg2, J1.pin2
  N8: U1.PB3(ADC3), R4.wiper
  N9: U1.GND, R4.leg1, J1.pin1, S2.2
  N10: U1.PB2(SCK_ADC1), S2.1
